// Logisim project Full Adder and ALU.circ as structural Verilog: 5 circuits, main circuit 16-bit ALU
module _4_bit_ALU (
  input  [3:0] A,
  input  [3:0] B,
  input  S2,
  input  S1,
  input  S0,
  output [3:0] OUT
);

  wire [3:0] _000, _001, _010, _011, _100, _101, _110, _111, not_1_out, not_2_out;

  assign not_1_out = ~B;  // NOT_Gate not_1, 4 bits wide
  _4_bit_Full_Adder u_4_bit_full_adder_1 (.in_1(A), .in_2(B), .in_3(1'b0), .out_4(_000));  // open: out_5
  _4_bit_Full_Adder u_4_bit_full_adder_2 (.in_1(A), .in_2(not_1_out), .in_3(1'b1), .out_4(_001));  // open: out_5
  assign _010 = A & 4'b0001;  // AND_Gate and_1, 4 bits wide
  assign not_2_out = ~A;  // NOT_Gate not_2, 4 bits wide
  _4_bit_Full_Adder u_4_bit_full_adder_3 (.in_1(not_2_out), .in_2(4'b0000), .in_3(1'b1), .out_4(_011));  // open: out_5
  _4_bit_Full_Adder u_4_bit_full_adder_4 (.in_1(A), .in_2(A), .in_3(1'b0), .out_4(_100));  // open: out_5
  assign _101 = A & B;  // AND_Gate and_2, 4 bits wide
  assign _110 = A | B;  // OR_Gate or_1, 4 bits wide
  assign _111 = A ^ B;  // XOR_Gate xor_1, 4 bits wide
  Multiplexer #(.select(3), .width(4), .disabled(0), .enable("false")) multiplexer_1 (
    .in0(_000), .in1(_001), .in2(_010), .in3(_011), .in4(_100), .in5(_101), .in6(_110), .in7(_111),
    .out(OUT), .sel({S2, S1, S0}));

  // Notes on the sheet:
  //   Op-Code
  //   000: Addition
  //   001: Subtraction
  //   010: isOddNumber
  //   100: Multiply by 2
  //   101: AND
  //   110: OR
  //   111: XOR
  //   011: 2's complement Negation
endmodule

module _1_bit_Full_Adder (
  input  in_1,
  input  in_2,
  input  in_3,
  output out_4,
  output out_5
);

  wire _1, _2, _3, _4, _5, _6, _7, not_1_out, not_2_out, not_3_out, not_4_out, not_5_out, not_6_out,
       not_7_out, not_8_out, not_9_out;

  and and_1 (_1, in_1, in_2, in_3);
  not not_1 (not_1_out, in_3);
  not not_2 (not_2_out, in_2);
  not not_3 (not_3_out, in_2);
  not not_4 (not_4_out, in_3);
  not not_5 (not_5_out, in_1);
  not not_6 (not_6_out, in_1);
  not not_7 (not_7_out, in_3);
  not not_8 (not_8_out, in_1);
  not not_9 (not_9_out, in_2);
  and and_2 (_2, in_1, in_2, not_1_out);
  and and_3 (_3, in_1, not_2_out, in_3);
  and and_4 (_4, in_1, not_3_out, not_4_out);
  and and_5 (_5, not_5_out, in_2, in_3);
  and and_6 (_6, not_6_out, in_2, not_7_out);
  and and_7 (_7, not_8_out, not_9_out, in_3);
  or or_1 (out_4, _5, _3, _2, _1);
  or or_2 (out_5, _1, _7, _6, _4);

  // Other names for the same wires on the sheet: A = in_1; B = in_2; CI = in_3; CO = out_4; OUT = out_5
endmodule

module _4_bit_Full_Adder (
  input  [3:0] in_1,
  input  [3:0] in_2,
  input  in_3,
  output [3:0] out_4,
  output out_5
);

  wire CI1, CI2, CI3;

  _1_bit_Full_Adder u_1_bit_full_adder_1 (.in_1(in_1[2]), .in_2(in_2[2]), .in_3(CI2), .out_4(CI3), .out_5(out_4[2]));
  _1_bit_Full_Adder u_1_bit_full_adder_2 (.in_1(in_1[0]), .in_2(in_2[0]), .in_3(in_3), .out_4(CI1), .out_5(out_4[0]));
  _1_bit_Full_Adder u_1_bit_full_adder_3 (.in_1(in_1[1]), .in_2(in_2[1]), .in_3(CI1), .out_4(CI2), .out_5(out_4[1]));
  _1_bit_Full_Adder u_1_bit_full_adder_4 (.in_1(in_1[3]), .in_2(in_2[3]), .in_3(CI3), .out_4(out_5), .out_5(out_4[3]));

  // Other names for the same wires on the sheet: CI0 = in_3; CO = out_5; A0 = in_1[0]; A1 = in_1[1]; A2 = in_1[2];
  //   A3 = in_1[3]; B0 = in_2[0]; B1 = in_2[1]; B2 = in_2[2]; B3 = in_2[3]; OUT0 = out_4[0]; OUT1 = out_4[1];
  //   OUT2 = out_4[2]; OUT3 = out_4[3]
endmodule

module _16_bit_Full_Adder (
  input  [15:0] in_1,
  input  [15:0] in_2,
  input  in_3,
  output [15:0] out_4,
  output out_5
);

  wire CI1, CI2, CI3;

  _4_bit_Full_Adder u_4_bit_full_adder_1 (
    .in_1(in_1[11:8]), .in_2(in_2[11:8]), .in_3(CI2), .out_4(out_4[11:8]), .out_5(CI3));
  _4_bit_Full_Adder u_4_bit_full_adder_2 (
    .in_1(in_1[3:0]), .in_2(in_2[3:0]), .in_3(in_3), .out_4(out_4[3:0]), .out_5(CI1));
  _4_bit_Full_Adder u_4_bit_full_adder_3 (
    .in_1(in_1[7:4]), .in_2(in_2[7:4]), .in_3(CI1), .out_4(out_4[7:4]), .out_5(CI2));
  _4_bit_Full_Adder u_4_bit_full_adder_4 (
    .in_1(in_1[15:12]), .in_2(in_2[15:12]), .in_3(CI3), .out_4(out_4[15:12]), .out_5(out_5));

  // Other names for the same wires on the sheet: CI0 = in_3; CO = out_5; A0[3:0] = in_1[3:0]; A1[3:0] = in_1[7:4];
  //   A2[3:0] = in_1[11:8]; A3[3:0] = in_1[15:12]; B0[3:0] = in_2[3:0]; B1[3:0] = in_2[7:4]; B2[3:0] = in_2[11:8];
  //   B3[3:0] = in_2[15:12]; OUT0[3:0] = out_4[3:0]; OUT1[3:0] = out_4[7:4]; OUT2[3:0] = out_4[11:8];
  //   OUT3[3:0] = out_4[15:12]
endmodule

module _16_bit_ALU (
  input  [15:0] A,
  input  [15:0] B,
  input  S2,
  input  S1,
  input  S0,
  output [15:0] OUT
);

  wire [15:0] _000, _001, _010, _011, _100, _101, _110, _111, not_1_out, not_2_out;

  assign not_1_out = ~B;  // NOT_Gate not_1, 16 bits wide
  _16_bit_Full_Adder u_16_bit_full_adder_1 (.in_1(A), .in_2(B), .in_3(1'b0), .out_4(_000));  // open: out_5
  _16_bit_Full_Adder u_16_bit_full_adder_2 (.in_1(A), .in_2(not_1_out), .in_3(1'b1), .out_4(_001));  // open: out_5
  assign _010 = A & 16'h1;  // AND_Gate and_1, 16 bits wide
  assign not_2_out = ~A;  // NOT_Gate not_2, 16 bits wide
  _16_bit_Full_Adder u_16_bit_full_adder_3 (
    .in_1(not_2_out), .in_2({16{1'b0}}), .in_3(1'b1), .out_4(_011));  // open: out_5
  _16_bit_Full_Adder u_16_bit_full_adder_4 (.in_1(A), .in_2(A), .in_3(1'b0), .out_4(_100));  // open: out_5
  assign _101 = A & B;  // AND_Gate and_2, 16 bits wide
  assign _110 = A | B;  // OR_Gate or_1, 16 bits wide
  assign _111 = A ^ B;  // XOR_Gate xor_1, 16 bits wide
  Multiplexer #(.select(3), .width(16), .disabled(0), .enable("false")) multiplexer_1 (
    .in0(_000), .in1(_001), .in2(_010), .in3(_011), .in4(_100), .in5(_101), .in6(_110), .in7(_111),
    .out(OUT), .sel({S2, S1, S0}));

  // Notes on the sheet:
  //   Op-Code
  //   000: Addition
  //   001: Subtraction
  //   010: isOddNumber
  //   100: Multiply by 2
  //   101: AND
  //   110: OR
  //   111: XOR
  //   011: 2's complement Negation
endmodule
