// Logisim project K-map state machine.circ as structural Verilog: 2 circuits, main circuit Tester
module Tester (
  input  G
);

  wire CLK_out, reduced_state_machine_1_w, reduced_state_machine_1_x, reduced_state_machine_1_y,
       reduced_state_machine_1_z, RST_out;

  Clock CLK (.out(CLK_out));
  Reduced_State_Machine reduced_state_machine_1 (
    .G(G), .Clock(CLK_out), .Reset(RST_out), .W(reduced_state_machine_1_w), .X(reduced_state_machine_1_x),
    .Y(reduced_state_machine_1_y), .Z(reduced_state_machine_1_z));
  LED led_1 (.in(reduced_state_machine_1_w));
  LED led_2 (.in(reduced_state_machine_1_x));
  LED led_3 (.in(reduced_state_machine_1_y));
  LED led_4 (.in(reduced_state_machine_1_z));
  Button RST (.out(RST_out));
endmodule

module Reduced_State_Machine (
  input  G,
  input  Clock,
  input  Reset,
  output W,
  output X,
  output Y,
  output Z
);

  wire and_1_out, and_2_out, and_3_out, and_4_out, and_5_out, and_6_out, and_7_out, and_8_out, and_9_out,
       and_10_out, and_11_out, and_12_out, N0, N1, N2, S1, S2;

  Register #(.width(3)) register_1 (.D({N2, N1, N0}), .Q({S2, S1, X}), .clk(Clock), .clr(Reset));  // open: en
  and and_1 (and_1_out, ~X, ~S1);  // AND_Gate
  and and_2 (and_2_out, ~G, ~S1);  // AND_Gate
  and and_3 (and_3_out, X, ~S1, ~S2);  // AND_Gate
  and and_4 (and_4_out, ~G, ~X, ~S2);  // AND_Gate
  and and_5 (and_5_out, G, ~X, S2);  // AND_Gate
  or or_1 (N0, and_1_out, and_2_out);
  or or_2 (N1, and_3_out, and_4_out, and_5_out);
  and and_6 (and_6_out, X, S1);
  and and_7 (and_7_out, G, S1);
  and and_8 (and_8_out, ~G, S2);  // AND_Gate
  or or_3 (N2, and_6_out, and_7_out, and_8_out);
  and and_9 (and_9_out, ~S1, ~S2);  // AND_Gate
  and and_10 (and_10_out, ~X, ~S1);  // AND_Gate
  and and_11 (and_11_out, ~X, ~S2);  // AND_Gate
  and and_12 (and_12_out, ~S1, ~S2);  // AND_Gate
  or or_4 (W, and_9_out, and_10_out);
  or or_5 (Y, and_11_out, and_12_out);
  not not_1 (Z, S1);

  // Other names for the same wires on the sheet: S0 = X; CLK = Clock; RST = Reset

  // Notes on the sheet:
  //   My name is:
  //   Daniel Kim
  //   and this is my reduced state machine
endmodule
