// Logisim project one-hot state machine.circ as structural Verilog: 2 circuits, main circuit One Hot State Machine
// S0
module One_Hot_State_Machine (
  input  G,
  input  Clock,
  input  Reset,
  output W,
  output X,
  output Y,
  output Z
);

  wire and_2_out, and_3_out, and_4_out, and_5_out, and_6_out, and_7_out, and_8_out, and_9_out, and_10_out,
       N0, N1, N2, N3, N4, N5, nor_1_out, S0, S1, S2, S3, S4, S5;

  nor nor_1 (nor_1_out, S0, S1, S2, S3, S4, S5);
  and and_1 (N1, S0, G);
  and and_2 (and_2_out, S1, G);
  and and_3 (and_3_out, S2, ~G);  // AND_Gate
  and and_4 (and_4_out, S0, ~G);  // AND_Gate
  and and_5 (and_5_out, S1, ~G);  // AND_Gate
  and and_6 (and_6_out, S4, G);
  Register #(.width(6)) register_1 (
    .D({N5, N4, N3, N2, N1, N0}), .Q({S5, S4, S3, S2, S1, S0}), .clk(Clock), .clr(Reset));  // open: en
  or or_1 (N0, nor_1_out, and_7_out);
  and and_7 (and_7_out, S5, G);
  or or_2 (N2, and_2_out, and_3_out);
  or or_3 (N3, and_4_out, and_5_out, and_6_out);
  and and_8 (and_8_out, S2, G);
  and and_9 (and_9_out, S4, ~G);  // AND_Gate
  and and_10 (and_10_out, S5, ~G);  // AND_Gate
  or or_4 (W, S0, S1, S4);
  or or_5 (X, S1, S3, S5);
  or or_6 (Y, S0, S1, S2);
  or or_7 (Z, S0, S1, S4, S5);
  or or_8 (N4, and_8_out, S3);
  or or_9 (N5, and_9_out, and_10_out);

  // Other names for the same wires on the sheet: CLK = Clock; RST = Reset

  // Notes on the sheet:
  //   My name is:
  //   Daniel Kim
  //   and this is my one-hot machine
endmodule

module Tester (
  input  G
);

  wire CLK_out, one_hot_state_machine_1_w, one_hot_state_machine_1_x, one_hot_state_machine_1_y,
       one_hot_state_machine_1_z, RST_out;

  Clock CLK (.out(CLK_out));
  LED led_1 (.in(one_hot_state_machine_1_w));
  One_Hot_State_Machine one_hot_state_machine_1 (
    .G(G), .Clock(CLK_out), .Reset(RST_out), .W(one_hot_state_machine_1_w), .X(one_hot_state_machine_1_x),
    .Y(one_hot_state_machine_1_y), .Z(one_hot_state_machine_1_z));
  LED led_2 (.in(one_hot_state_machine_1_x));
  LED led_3 (.in(one_hot_state_machine_1_y));
  LED led_4 (.in(one_hot_state_machine_1_z));
  Button RST (.out(RST_out));
endmodule
